# Fritzing sketch skellington2 (saved by Fritzing 1.0.1rc)
stripboards: 2

parts:
  Part1 = Thumb Joystick
  J1 = Basic Servo
  S1 = Round Pushbutton
  Part2 = TRRS 3.5mm Jack Breakout
  DFPlayer_Mini1 = DFPlayer MINI [package="DIP (Dual Inline) [THT]"]
  U1 = V_REG_LD1117VXX [package=78xxl]
  Part3 = LCD1602-I2C
  J2 = Power Jack [package=power_jack_smd]
  J3 = Basic Servo
  J4 = Basic Servo
  KEYPAD1 = Membrane Matrix Keypad
  Mod1 = Raspberry Pi Pico

nets:
  GND: Part1.GND, J1.gnd, S1.leg1, Part2.SLEEVE, DFPlayer_Mini1.GND#6, U1.GND, Part3.GND, J2.GND, J3.gnd, J4.gnd, KEYPAD1.5, Mod1.pin_3, Mod1.pin_8, Mod1.pin_13, Mod1.pin_18, Mod1.pin_23, Mod1.pin_28, Mod1.pin_33, Mod1.pin_38
  N1: Part1.HORZ, Mod1.pin_31
  N2: Part1.VERT, Mod1.pin_32
  VCC: Part1.VCC, Part3.VCC, Mod1.pin_36
  VCC_2: J1.vcc, U1.IN, J2.PWR, J3.vcc, J4.vcc, Mod1.pin_39
  N3: J1.pulse, Mod1.pin_4
  N4: S1.leg0, Mod1.pin_1
  N5: Part2.RING1, DFPlayer_Mini1.DAC_R
  N6: Part2.TIP, DFPlayer_Mini1.DAC_L
  N7: DFPlayer_Mini1.VCC, U1.OUT
  N8: DFPlayer_Mini1.RX, Mod1.pin_25
  N9: DFPlayer_Mini1.TX, Mod1.pin_21
  N10: J3.pulse, Mod1.pin_5
  N11: J4.pulse, Mod1.pin_2
  N12: KEYPAD1.1, Mod1.pin_9
  N13: KEYPAD1.2, Mod1.pin_6
  N14: KEYPAD1.3, Mod1.pin_11
  N15: KEYPAD1.4, Mod1.pin_7
  N16: KEYPAD1.6, Mod1.pin_12
  N17: KEYPAD1.7, Mod1.pin_10

custom parts:
  DFPlayer MINI: MP3 module by DFRobot.com for playing Music from an SD-Card. Supports WAV and MP3 files.
  LCD1602-I2C: A standard character display, usually with 2x16 characters. Comes in many colors with LCM1602 IIC attached.
  Membrane Matrix Keypad: Membrane Matrix 3x4 Keypad
  Raspberry Pi Pico: Raspberry Pi Pico. Based around the RP2040 microcontroller the Pico is a low cost microcontroller device bringing Raspberry Pi quality, cost, and easy of use to the microcontroller space. Jan 2021, Split part in to two versions: SMD (this one) and tht. This one is single sided and uses the castellation pads to solder the module to the board (no holes, other than for the USB connector!). The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
